# Fritzing sketch 7SegmentosSketch (saved by Fritzing 0.9.8b)
breadboards: 1

parts:
  Raspberry_Pi_1 = Raspberry Pi 3 [part_number=RPI-3-V1.2]
  U2 = 7-SEGMENT-DISPLAY [package=7-segment-display]
  R1 = Resistor [tolerance=±5% resistance=220 package="2512 [SMD]"]
  R2 = Resistor [tolerance=±5% resistance=220 package="2512 [SMD]"]
  R3 = Resistor [tolerance=±5% resistance=220 package="2512 [SMD]"]
  R4 = Resistor [tolerance=±5% resistance=220 package="2512 [SMD]"]
  R5 = Resistor [tolerance=±5% resistance=220 package="2512 [SMD]"]
  R6 = Resistor [tolerance=±5% resistance=220 package="2512 [SMD]"]
  R7 = Resistor [tolerance=±5% resistance=220 package="2512 [SMD]"]
  R8 = Resistor [tolerance=±5% resistance=220 package="2512 [SMD]"]

nets:
  N1: Raspberry_Pi_1.GPIO7, R6.Pin_0
  N2: Raspberry_Pi_1.GPIO8, R8.Pin_0
  N3: Raspberry_Pi_1.GPIO25, R7.Pin_0
  N4: Raspberry_Pi_1.GPIO24, R5.Pin_0
  N5: Raspberry_Pi_1.GPIO23, R3.Pin_0
  N6: Raspberry_Pi_1.GPIO18, R4.Pin_0
  N7: Raspberry_Pi_1.GPIO15, R2.Pin_0
  N8: Raspberry_Pi_1.GPIO14, R1.Pin_0
  N9: Raspberry_Pi_1.GND, U2.C, U2.F
  N10: U2.E, R8.Pin_1
  N11: U2.D, R5.Pin_1
  N12: U2.G1, R3.Pin_1
  N13: U2.DP, R4.Pin_1
  N14: U2.B, R6.Pin_1
  N15: U2.A, R2.Pin_1
  N16: U2.G2, R1.Pin_1
  N17: U2.G, R7.Pin_1
