# Fritzing sketch 7SegmentosSketchSinResistencia (saved by Fritzing 0.9.8b)
breadboards: 1

parts:
  Raspberry_Pi_1 = Raspberry Pi 3 [part_number=RPI-3-V1.2]
  U2 = 7-SEGMENT-DISPLAY [package=7-segment-display]

nets:
  N1: Raspberry_Pi_1.GPIO7, U2.B
  N2: Raspberry_Pi_1.GPIO8, U2.E
  N3: Raspberry_Pi_1.GPIO25, U2.G
  N4: Raspberry_Pi_1.GPIO24, U2.D
  N5: Raspberry_Pi_1.GPIO23, U2.G1
  N6: Raspberry_Pi_1.GPIO18, U2.DP
  N7: Raspberry_Pi_1.GPIO15, U2.A
  N8: Raspberry_Pi_1.GPIO14, U2.G2
  N9: Raspberry_Pi_1.GND, U2.C, U2.F
