# Fritzing sketch DistanceSensorSketch (saved by Fritzing 0.9.8b)
breadboards: 1

parts:
  Raspberry_Pi_1 = Raspberry Pi 3 [part_number=RPI-3-V1.2]
  HC-SR04_Sensor_1 = HC-SR04 Ultrasonic Distance Sensor
  R1 = Resistor [tolerance=±5% resistance=2.2k package="1206 [SMD]"]
  R2 = Resistor [tolerance=±5% resistance=1k package="1206 [SMD]"]
  8_Channel_Relay1 = 8 Channel Power Relay
  LED1 = LED - 5mm [color="White (8000K)" current=0.030 package="5 mm [THT]"]
  LED2 = LED - 5mm [color="Green (555nm)" current=0.030 package="5 mm [THT]"]
  LED3 = LED - 5mm [color="Blue (430nm)" current=0.030 package="5 mm [THT]"]

nets:
  3V3: Raspberry_Pi_1.3v3, Raspberry_Pi_1.3V3, LED1.anode, LED2.anode, LED3.anode
  N1: Raspberry_Pi_1.GIPO4, HC-SR04_Sensor_1.TRIG
  N2: Raspberry_Pi_1.GIPO17, R1.Pin_1, R2.Pin_1
  N3: Raspberry_Pi_1.GIPO27, 8_Channel_Relay1.IN1
  GND: Raspberry_Pi_1.GND, HC-SR04_Sensor_1.GND, 8_Channel_Relay1.GND, LED1.cathode, LED2.cathode, LED3.cathode
  VCC: Raspberry_Pi_1.5V, HC-SR04_Sensor_1.VCC, R2.Pin_0, 8_Channel_Relay1.VCC
  N4: HC-SR04_Sensor_1.ECHO, R1.Pin_0

custom parts:
  8 Channel Power Relay: An 8 channel power relay. The module operates at 5V.
