# Fritzing sketch SonarConLeds (saved by Fritzing 0.9.8b)
breadboards: 1

parts:
  Raspberry_Pi_1 = Raspberry Pi 3 [part_number=RPI-3-V1.2]
  HC-SR04_Sensor_1 = HC-SR04 Ultrasonic Distance Sensor
  R1 = Resistor [tolerance=±5% resistance=100 package="0402 [SMD]"]
  R2 = Resistor [tolerance=±5% resistance=100 package="0402 [SMD]"]
  LED1 = smd LED [color="Green (560nm)" package="0805 [SMD]"]
  LED2 = smd LED [color="Blue (525nm)" package="0805 [SMD]"]
  R3 = Resistor [tolerance=±5% resistance=1k package="0402 [SMD]"]
  R4 = Resistor [tolerance=±5% resistance=2k package="0402 [SMD]"]

nets:
  GND: Raspberry_Pi_1.GPIO3, Raspberry_Pi_1.GND, HC-SR04_Sensor_1.GND, LED1.cathode, LED2.cathode, R4.Pin_0
  N1: Raspberry_Pi_1.GPIO4, HC-SR04_Sensor_1.TRIG
  N2: Raspberry_Pi_1.GPIO17, R3.Pin_1, R4.Pin_1
  N3: Raspberry_Pi_1.GPIO27, R2.Pin_0
  N4: Raspberry_Pi_1.GPIO22, R1.Pin_0
  5V: Raspberry_Pi_1.5V, HC-SR04_Sensor_1.VCC
  N5: HC-SR04_Sensor_1.ECHO, R3.Pin_0
  N6: R1.Pin_1, LED1.anode
  N7: R2.Pin_1, LED2.anode
