# Fritzing sketch sensorTemperatura (saved by Fritzing 0.9.8b)
breadboards: 1

parts:
  Raspberry_Pi_1 = Raspberry Pi 3 [part_number=RPI-3-V1.2]
  DHT1 = DHT11 Humitidy and Temperature Sensor (3 pins)
  R1 = Resistor [tolerance=±5% resistance=220 package="2512 [SMD]"]

nets:
  3V3: Raspberry_Pi_1.3v3, DHT1.VDD, R1.Pin_1
  N1: Raspberry_Pi_1.GPIO4, DHT1.DATA, R1.Pin_0
  GND: Raspberry_Pi_1.GND, DHT1.GND

custom parts:
  DHT11 Humitidy and Temperature Sensor (3 pins): DHT11 Humidity and Temperature Sensor (3 pins) from the design created by John De Cristofaro for Adafruit Industries.
