# Fritzing sketch 28BYJ-48-driver_and_motor (saved by Fritzing 0.9.8b)

parts:
  Driver1 = 28BYJ-48 Driver Module [part_number=ULN2003 package=THT]
  SM1 = 28BYJ-48 Stepper Motor [part_number=28BYJ-48]
  Raspberry_Pi_1 = Raspberry Pi 3 [part_number=RPI-3-V1.2]

nets:
  N1: Driver1.IN1, Raspberry_Pi_1.GPIO4
  N2: Driver1.IN2, Raspberry_Pi_1.GPIO17
  N3: Driver1.IN3, Raspberry_Pi_1.GPIO27
  N4: Driver1.IN4, Raspberry_Pi_1.GPIO22
  GND: Driver1.GND, Raspberry_Pi_1.GND
  N5: Driver1.Vmotor, Raspberry_Pi_1.5V
  N6: Driver1.blue-pin, SM1.blue-pin
  N7: Driver1.pink-pin, SM1.pink-pin
  N8: Driver1.yellow-pin, SM1.yellow-pin
  N9: Driver1.orange-pin, SM1.orange-pin
  N10: Driver1.red-pin, SM1.red-pin

custom parts:
  28BYJ-48 Driver Module: Generic male header
  28BYJ-48 Stepper Motor: Unipolar Stepper Motor 28BYJ-48 Top coil - pink & orange Bottom coil - blue & yellow Common rail - red Connector pins: blue - pink - yellow - orange - red
